# Fritzing sketch yai-water_tank (saved by Fritzing 0.9.4)
breadboards: 1

parts:
  HC-SR04_Sensor_1 = HC-SR04 Ultrasonic Distance Sensor
  U2 = NodeMCU V3.0

nets:
  VCC: HC-SR04_Sensor_1.VCC, U2.Vin
  N1: HC-SR04_Sensor_1.TRIG, U2.D2
  N2: HC-SR04_Sensor_1.ECHO, U2.D1
  N3: HC-SR04_Sensor_1.GND, U2.GND#6, U2.GND#13, U2.GND#16, U2.GND#33

custom parts:
  NodeMCU V3.0: ESP8266 based NodeMCU
